# Fritzing sketch CarCompanionPCBv1 (saved by Fritzing 0.9.2b)
circuit board: 5cm x 5cm

parts:
  R14 = Resistor [tolerance=±5% resistance=10k package=THT]
  R15 = Resistor [tolerance=±5% resistance=10k package=THT]
  R16 = Resistor [tolerance=±5% resistance=10k package=THT]
  R17 = Resistor [tolerance=±5% resistance=270 package=THT]
  R18 = Resistor [tolerance=±5% resistance=270 package=THT]
  R19 = Resistor [tolerance=±5% resistance=270 package=THT]
  R20 = Resistor [tolerance=±5% resistance=270 package=THT]
  R21 = Resistor [tolerance=±5% resistance=220 package=THT]
  R22 = Resistor [tolerance=±5% resistance=270 package=THT]
  R23 = Resistor [tolerance=±5% resistance=10k package=THT]
  R24 = Resistor [tolerance=±5% resistance=270 package=THT]
  R25 = Resistor [tolerance=±5% resistance=270 package=THT]
  Status_LED1 = LED - 3mm [color="Red (633nm)" package="3 mm [THT]"]
  12Vin = Screw terminal - 2 pins [package=THT]
  D9 = Screw terminal - 2 pins [package=THT]
  D5 = Screw terminal - 2 pins [package=THT]
  D10 = Screw terminal - 2 pins [package=THT]
  D11 = Screw terminal - 2 pins [package=THT]
  D12btn = female pin header, 2 pins [form="♀ (female)"]
  LockOut = female pin header, 2 pins [form="♀ (female)"]
  LckBtn = female pin header, 2 pins [form="♀ (female)"]
  D4btn = female pin header, 2 pins [form="♀ (female)"]
  Part3 = Arduino Nano (Rev3.0)
  U8 = TRANSISTOR_NPN [package=sot23]
  U13 = TRANSISTOR_NPN [package=sot23]
  U14 = TRANSISTOR_NPN [package=sot23]
  U11 = TRANSISTOR_NPN [package=sot23]
  U10 = TRANSISTOR_NPN [package=sot23]
  C1 = Tantalum Capacitor [capacitance=100μF voltage=35V package="100 mil [THT, tantalum]"]
  RST = female pin header, 2 pins [form="♀ (female)"]
  ExpansionPort = female pin header, 9 pins [form="♀ (female)"]
  LDO_Reg = Voltage Regulator [package=to-92]
  A7btn = female pin header, 2 pins [form="♀ (female)"]
  UnlockOut = female pin header, 2 pins [form="♀ (female)"]
  Part4 = Bluetooth HC-05

nets:
  N1: R14.Pin_0, D12btn.pin2, Part3.D12/MISO
  N2: R14.Pin_1, R15.Pin_1, R16.Pin_0, R23.Pin_1, Part3.5V, U10.C, ExpansionPort.pin7, LDO_Reg.OUT
  N3: R15.Pin_0, D4btn.pin2, Part3.D4
  N4: R16.Pin_1, Part3.A7, A7btn.pin1
  N5: R17.Pin_0, Part3.D7
  N6: R17.Pin_1, UnlockOut.pin1
  N7: R18.Pin_0, Part3.D5
  N8: R18.Pin_1, U11.C
  N9: R19.Pin_0, Part3.D8
  N10: R19.Pin_1, LockOut.pin1
  N11: R20.Pin_0, Part3.D10
  N12: R20.Pin_1, U13.B
  N13: R21.Pin_0, Part3.D13/SCK
  N14: R21.Pin_1, Status_LED1.anode
  N15: R22.Pin_0, U10.B
  N16: R22.Pin_1, Part3.A1
  N17: R23.Pin_0, LckBtn.pin1, Part3.D6
  N18: R24.Pin_0, Part3.D9
  N19: R24.Pin_1, U8.B
  N20: R25.Pin_0, Part3.D11/MOSI
  N21: R25.Pin_1, U14.B
  GND: Status_LED1.cathode, 12Vin.pin2, D12btn.pin1, LockOut.pin2, LckBtn.pin2, D4btn.pin1, Part3.GND, U8.E, U13.E, U14.E, U11.E, C1.-, RST.pin2, ExpansionPort.pin9, LDO_Reg.GND, A7btn.pin2, UnlockOut.pin2, Part4.GND
  12v: 12Vin.pin1, D9.pin1, D5.pin1, D10.pin1, D11.pin2, C1.+, ExpansionPort.pin1, LDO_Reg.IN
  N22: D9.pin2, U8.C
  N23: D5.pin2, U11.B
  N24: D10.pin2, U13.C
  N25: D11.pin1, U14.C
  N26: Part3.RESET, RST.pin1
  N27: Part3.D2, Part4.RXD
  N28: Part3.D3, Part4.TXD
  N29: Part3.A6, ExpansionPort.pin2
  N30: Part3.A5, ExpansionPort.pin3
  N31: Part3.A4, ExpansionPort.pin4
  N32: Part3.A3, ExpansionPort.pin5
  N33: Part3.A2, ExpansionPort.pin6
  N34: Part3.A0, Part4.Key
  N35: Part3.3V3, ExpansionPort.pin8
  N36: U10.E, Part4.VCC

notes:
  An open source CarCompanion.
  github.com/jabelone/CarCompanion
  - +
  12Vin
  Lock
  Unlock
  D5
  G
  ^RST
  D4
  GND
  LkBtn
  D9
  D11
  D10
  CarCompanion v1
  3v3
  5v
  A6
  A5
  A4
  A3
  A2
  12v
