# Fritzing sketch CarCompanionSchematic (saved by Fritzing 0.9.2b)
circuit board: 6cm x 6cm

parts:
  Part2 = Arduino Nano (Rev3.0)
  U1 = TRANSISTOR_NPN_2 [package=to-92]
  U2 = TRANSISTOR_NPN_2 [package=to-92]
  U5 = TRANSISTOR_NPN_2 [package=to-92]
  U6 = TRANSISTOR_NPN_2 [package=to-92]
  S4 = SWITCH-MOMENTARY-2 [package=tactile-pth]
  J1 = Screw terminal - 2 pins [package=THT]
  J2 = Screw terminal - 2 pins [package=THT]
  J5 = Screw terminal - 2 pins [package=THT]
  J6 = Screw terminal - 2 pins [package=THT]
  J7 = Screw terminal - 2 pins [package=THT]
  J8 = Screw terminal - 2 pins [package=THT]
  J9 = Screw terminal - 2 pins [package=THT]
  J3 = Screw terminal - 2 pins [package=THT]
  J4 = Screw terminal - 2 pins [package=THT]
  U4 = TRANSISTOR_NPN_2 [package=to-92]
  U3 = TRANSISTOR_NPN_2 [package=to-92]
  J10 = Screw terminal - 2 pins [package=THT]
  R3 = Resistor [tolerance=±5% resistance=270 package=THT]
  R5 = Resistor [tolerance=±5% resistance=270 package=THT]
  R8 = Resistor [tolerance=±5% resistance=10k package=THT]
  R11 = Resistor [tolerance=±5% resistance=270 package=THT]
  R1 = Resistor [tolerance=±5% resistance=220 package=THT]
  R4 = Resistor [tolerance=±5% resistance=270 package=THT]
  R6 = Resistor [tolerance=±5% resistance=270 package=THT]
  R9 = Resistor [tolerance=±5% resistance=270 package=THT]
  R7 = Resistor [tolerance=±5% resistance=270 package=THT]
  R10 = Resistor [tolerance=±5% resistance=10k package=THT]
  R2 = Resistor [tolerance=±5% resistance=10k package=THT]
  Status_LED = LED - 3mm [color="Red (633nm)" package="3 mm [THT]"]
  U7 = TRANSISTOR_NPN_2 [package=to-92]
  Part1 = Bluetooth HC-05

nets:
  12gnd/GND: Part2.GND, U1.E, U2.E, U5.E, U6.E, S4.2, J7.pin1, J8.pin1, J9.pin1, U4.E, U3.E, J10.pin2, Status_LED.cathode, Part1.GND
  N1: Part2.D2, Part1.RXD
  N2: Part2.D3, Part1.TXD
  N3: Part2.D4, J8.pin2, R10.Pin_0
  N4: Part2.D5, R9.Pin_0
  N5: Part2.D6, J9.pin2, R8.Pin_0
  N6: Part2.D7, R7.Pin_0
  N7: Part2.D8, R6.Pin_0
  N8: Part2.D9, R5.Pin_0
  N9: Part2.D10, R4.Pin_0
  N10: Part2.D11/MOSI, R3.Pin_0
  N11: Part2.D12/MISO, J7.pin2, R2.Pin_0
  12v: Part2.VIN, J1.pin1, J2.pin1, J5.pin1, J6.pin1, J3.pin1, J4.pin1, J10.pin1
  N12: Part2.RESET, S4.1
  N13: Part2.A1, R11.Pin_1
  N14: Part2.A0, Part1.Key
  N15: Part2.D13/SCK, R1.Pin_0
  N16: U1.C, J1.pin2
  N17: U1.B, R3.Pin_1
  N18: U2.C, J2.pin2
  N19: U2.B, R4.Pin_1
  N20: U5.C, J5.pin2
  N21: U5.B, R7.Pin_1
  N22: U6.C, J6.pin2
  N23: U6.B, R9.Pin_1
  N24: J3.pin2, U3.C
  N25: J4.pin2, U4.C
  N26: U4.B, R6.Pin_1
  N27: U3.B, R5.Pin_1
  N28: R8.Pin_1, R10.Pin_1, R2.Pin_1, U7.C
  N29: R11.Pin_0, U7.B
  N30: R1.Pin_1, Status_LED.anode
  N31: U7.E, Part1.VCC

notes:
  CarCompanion 1.0
  VIN
